# Fritzing sketch CoffeeSensor (saved by Fritzing 0.9.3b)

parts:
  HX711 = HX711 Weighing Sensor Module
  IR = fc-51 [package=THT]
  Raspberry_Pi_3 = Raspberry Pi 3 [part_number=RPI-3-V1.2]

nets:
  VCC: HX711.VCC, Raspberry_Pi_3.5V
  GND: HX711.GND, IR.pin2, Raspberry_Pi_3.GND
  N1: HX711.DO/RX, Raspberry_Pi_3.GIPO24
  N2: HX711.CK/TX, Raspberry_Pi_3.GIPO23
  N3: IR.pin1, Raspberry_Pi_3.GIPO5
  N4: IR.pin3, Raspberry_Pi_3.3V3

notes:
  connected to weighing cell
