# Fritzing sketch CoffeeSensorEsp (saved by Fritzing 0.9.3b)

parts:
  HX711 = HX711 Weighing Sensor Module
  IR = fc-51 [package=THT]
  U1 = NodeMCU V3.0

nets:
  VCC: HX711.VCC, IR.pin3, U1.Vin
  GND: HX711.GND, IR.pin2, U1.GND
  N1: HX711.DO/RX, U1.D3
  N2: HX711.CK/TX, U1.D2
  N3: IR.pin1, U1.D1

notes:
  connected to weighing cell

custom parts:
  NodeMCU V3.0: ESP8266 based NodeMCU
